// Logisim project ALUv1.circ as structural Verilog
module eightbitadder (
  input  Cin,
  input  Subtract,
  input  [7:0] A,
  input  [7:0] B,
  output [7:0] out_5,
  output out_6
);

  wire onebitadder_1_cout, onebitadder_2_cout, onebitadder_3_cout, onebitadder_4_cout, onebitadder_5_cout,
       onebitadder_6_cout, onebitadder_7_cout;

  onebitadder onebitadder_1 (.A(A[0]), .B(B[0]), .Sub(Subtract), .Cin(Cin), .Cout(onebitadder_1_cout), .Sum(out_5[0]));
  onebitadder onebitadder_2 (
    .A(A[1]), .B(B[1]), .Sub(Subtract), .Cout(onebitadder_2_cout), .Sum(out_5[1]));  // open: Cin
  onebitadder onebitadder_3 (
    .A(A[2]), .B(B[2]), .Sub(Subtract), .Cin(onebitadder_2_cout), .Cout(onebitadder_3_cout), .Sum(out_5[2]));
  onebitadder onebitadder_4 (
    .A(A[3]), .B(B[3]), .Sub(Subtract), .Cin(onebitadder_3_cout), .Cout(onebitadder_4_cout), .Sum(out_5[3]));
  onebitadder onebitadder_5 (
    .A(A[4]), .B(B[4]), .Sub(Subtract), .Cin(onebitadder_4_cout), .Cout(onebitadder_5_cout), .Sum(out_5[4]));
  onebitadder onebitadder_6 (
    .A(A[5]), .B(B[5]), .Sub(Subtract), .Cin(onebitadder_5_cout), .Cout(onebitadder_6_cout), .Sum(out_5[5]));
  onebitadder onebitadder_7 (
    .A(A[6]), .B(B[6]), .Sub(Subtract), .Cin(onebitadder_6_cout), .Cout(onebitadder_7_cout), .Sum(out_5[6]));
  onebitadder onebitadder_8 (.A(A[7]), .B(B[7]), .Sub(Subtract), .Cout(out_6), .Sum(out_5[7]));  // open: Cin
endmodule

module onebitadder (
  input  A,
  input  B,
  input  Sub,
  input  Cin,
  output Cout,
  output Sum
);

  wire and_1_out, and_2_out, xor_1_out, xor_2_out;

  xor xor_1 (xor_1_out, B, Sub);
  xor xor_2 (xor_2_out, A, xor_1_out);
  and and_1 (and_1_out, A, xor_1_out);
  // XOR_Gate xor_3 has open pins: in0=A, in1=xor_1_out, out=open
  xor xor_4 (Sum, xor_2_out, Cin);
  or or_1 (Cout, and_1_out, and_2_out);
  buf and_2 (and_2_out, Cin);  // AND_Gate
endmodule
